// Logisim project master.circ as structural Verilog: 17 circuits, main circuit FullAdder
module HalfAdder (
  input  A,
  input  B,
  output Sum,
  output Cout
);

  xor xor_1 (Sum, A, B);
  and and_1 (Cout, A, B);
endmodule

module FullAdder (
  input  A,
  input  B,
  input  Cin,
  output Sum,
  output Cout
);

  wire and_1_out, and_2_out, and_3_out, xor_1_out;

  and and_1 (and_1_out, B, Cin);
  and and_2 (and_2_out, A, Cin);
  and and_3 (and_3_out, A, B);
  or or_1 (Cout, and_1_out, and_2_out, and_3_out);
  xor xor_1 (xor_1_out, A, B);
  xor xor_2 (Sum, xor_1_out, Cin);
endmodule

module FullSubtractor (
  input  A,
  input  B,
  input  Bin,
  output Sum,
  output Bout
);

  wire and_1_out, and_2_out, and_3_out, not_1_out, not_2_out, xor_1_out;

  and and_1 (and_1_out, B, Bin);
  not not_1 (not_1_out, A);
  and and_2 (and_2_out, not_1_out, Bin);
  not not_2 (not_2_out, A);
  and and_3 (and_3_out, not_2_out, B);
  or or_1 (Bout, and_1_out, and_2_out, and_3_out);
  xor xor_1 (xor_1_out, A, B);
  xor xor_2 (Sum, xor_1_out, Bin);
endmodule

module OnesComp (
  input  [3:0] A,
  output [3:0] R
);

  not not_1 (R[0], A[0]);
  not not_2 (R[1], A[1]);
  not not_3 (R[2], A[2]);
  not not_4 (R[3], A[3]);
endmodule

module TwosComp (
  input  [3:0] A,
  output [3:0] R,
  output Overflow
);

  wire fulladder_1_cout, fulladder_2_cout, fulladder_3_cout;
  wire [3:0] onescomp_1_r;

  OnesComp onescomp_1 (.A(A), .R(onescomp_1_r));
  FullAdder fulladder_1 (.A(1'b1), .B(onescomp_1_r[0]), .Sum(R[0]), .Cout(fulladder_1_cout));  // open: Cin
  FullAdder fulladder_2 (.A(onescomp_1_r[1]), .Cin(fulladder_1_cout), .Sum(R[1]), .Cout(fulladder_2_cout));  // open: B
  FullAdder fulladder_3 (.A(onescomp_1_r[2]), .Cin(fulladder_2_cout), .Sum(R[2]), .Cout(fulladder_3_cout));  // open: B
  FullAdder fulladder_4 (.A(onescomp_1_r[3]), .Cin(fulladder_3_cout), .Sum(R[3]), .Cout(Overflow));  // open: B
endmodule

module FourBitAdder (
  input  [3:0] Add1,
  input  [3:0] Add2,
  output [3:0] AddOut
);

  wire fulladder_2_cout, fulladder_3_cout, fulladder_4_cout;

  FullAdder fulladder_1 (.A(Add1[3]), .B(Add2[3]), .Cin(fulladder_2_cout), .Sum(AddOut[3]));  // open: Cout
  FullAdder fulladder_2 (.A(Add1[2]), .B(Add2[2]), .Cin(fulladder_3_cout), .Sum(AddOut[2]), .Cout(fulladder_2_cout));
  FullAdder fulladder_3 (.A(Add1[1]), .B(Add2[1]), .Cin(fulladder_4_cout), .Sum(AddOut[1]), .Cout(fulladder_3_cout));
  FullAdder fulladder_4 (.A(Add1[0]), .B(Add2[0]), .Sum(AddOut[0]), .Cout(fulladder_4_cout));  // open: Cin
endmodule

module FourBitSubtractor (
  input  [3:0] Subtract1,
  input  [3:0] Subtract2,
  output [3:0] SubtractOut
);

  wire fullsubtractor_2_bout, fullsubtractor_3_bout, fullsubtractor_4_bout;

  FullSubtractor fullsubtractor_1 (
    .A(Subtract1[3]), .B(Subtract2[3]), .Bin(fullsubtractor_2_bout), .Sum(SubtractOut[3]));  // open: Bout
  FullSubtractor fullsubtractor_2 (
    .A(Subtract1[2]), .B(Subtract2[2]), .Bin(fullsubtractor_3_bout), .Sum(SubtractOut[2]),
    .Bout(fullsubtractor_2_bout));
  FullSubtractor fullsubtractor_3 (
    .A(Subtract1[1]), .B(Subtract2[1]), .Bin(fullsubtractor_4_bout), .Sum(SubtractOut[1]),
    .Bout(fullsubtractor_3_bout));
  FullSubtractor fullsubtractor_4 (
    .A(Subtract1[0]), .B(Subtract2[0]), .Sum(SubtractOut[0]), .Bout(fullsubtractor_4_bout));  // open: Bin
endmodule

module SR_Latch (
  input  Reset,
  input  Set,
  output Q,
  output NOT_Q
);

  nor nor_1 (Q, Reset, NOT_Q);
  nor nor_2 (NOT_Q, Q, Set);
endmodule

module Clocked_SR_Latch (
  input  Set,
  input  Reset,
  input  Clk,
  output Q,
  output NOT_Q
);

  wire nand_1_out, nand_2_out;

  nand nand_1 (nand_1_out, Set, Clk);
  nand nand_2 (nand_2_out, Clk, Reset);
  nand nand_3 (Q, nand_1_out, NOT_Q);
  nand nand_4 (NOT_Q, Q, nand_2_out);
endmodule

module D_Latch (
  input  D,
  input  Clk,
  output Q,
  output NOT_Q
);

  wire not_1_out;

  not not_1 (not_1_out, D);
  Clocked_SR_Latch clocked_sr_latch_1 (.Set(D), .Reset(not_1_out), .Clk(Clk), .Q(Q), .NOT_Q(NOT_Q));
endmodule

module SR_FlipFlop (
  input  Set,
  input  Reset,
  input  Clk,
  output Q,
  output NOT_Q
);

  wire clocked_sr_latch_1_not_q, clocked_sr_latch_1_q, not_1_out, not_2_out;

  not not_1 (not_1_out, Clk);
  Clocked_SR_Latch clocked_sr_latch_1 (
    .Set(Set), .Reset(Reset), .Clk(not_1_out), .Q(clocked_sr_latch_1_q), .NOT_Q(clocked_sr_latch_1_not_q));
  not not_2 (not_2_out, not_1_out);
  Clocked_SR_Latch clocked_sr_latch_2 (
    .Set(clocked_sr_latch_1_q), .Reset(clocked_sr_latch_1_not_q), .Clk(not_2_out), .Q(Q), .NOT_Q(NOT_Q));

  // Notes on the sheet:
  //   Rising Edge
  //   Falling Edge
endmodule

module D_FlipFlop (
  input  D,
  input  Clk,
  output Q,
  output NOT_Q
);

  wire d_latch_1_not_q, d_latch_1_q, not_1_out, not_2_out;

  not not_1 (not_1_out, Clk);
  D_Latch d_latch_1 (.D(D), .Clk(not_1_out), .Q(d_latch_1_q), .NOT_Q(d_latch_1_not_q));
  not not_2 (not_2_out, not_1_out);
  Clocked_SR_Latch clocked_sr_latch_1 (
    .Set(d_latch_1_q), .Reset(d_latch_1_not_q), .Clk(not_2_out), .Q(Q), .NOT_Q(NOT_Q));

  // Notes on the sheet:
  //   Rising Edge
  //   Falling Edge
endmodule

module JK_FlipFlop (
  input  J,
  input  K,
  input  Clk,
  output Q,
  output NOT_Q
);

  wire and_1_out, and_2_out, not_1_out, or_1_out;

  not not_1 (not_1_out, K);
  and and_1 (and_1_out, NOT_Q, J);
  or or_1 (or_1_out, and_1_out, and_2_out);
  and and_2 (and_2_out, not_1_out, Q);
  D_Flip_Flop d_ff_1 (.D(or_1_out), .clk(Clk), .Q(Q), .Qn(NOT_Q));  // open: preset, reset
endmodule

module T_FlipFlop (
  input  T,
  input  Clk,
  output Q,
  output NOT_Q
);

  wire xor_1_out;

  xor xor_1 (xor_1_out, Q, T);
  D_Flip_Flop d_ff_1 (.D(xor_1_out), .clk(Clk), .Q(Q), .Qn(NOT_Q));  // open: preset, reset
endmodule

module TwoBitRegister (
  input  In1,
  input  In0,
  input  Reset,
  input  Clk,
  output Y1,
  output Y0
);

  D_Flip_Flop A1 (.D(In1), .clk(Clk), .Q(Y1), .reset(Reset));  // open: Qn, preset
  D_Flip_Flop A0 (.D(In0), .clk(Clk), .Q(Y0), .reset(Reset));  // open: Qn, preset
endmodule

module FourBitRegister (
  input  In3,
  input  In2,
  input  In1,
  input  In0,
  input  Reset,
  input  Clk,
  output Y3,
  output Y2,
  output Y1,
  output Y0
);

  D_Flip_Flop A3 (.D(In3), .clk(Clk), .Q(Y3), .reset(Reset));  // open: Qn, preset
  D_Flip_Flop A2 (.D(In2), .clk(Clk), .Q(Y2), .reset(Reset));  // open: Qn, preset
  D_Flip_Flop A1 (.D(In1), .clk(Clk), .Q(Y1), .reset(Reset));  // open: Qn, preset
  D_Flip_Flop A0 (.D(In0), .clk(Clk), .Q(Y0), .reset(Reset));  // open: Qn, preset
endmodule

module FourBitRegisterWithLoad (
  input  In3,
  input  In2,
  input  In1,
  input  In0,
  input  Load,
  input  Reset,
  input  Clk,
  output Y3,
  output Y2,
  output Y1,
  output Y0
);

  wire multiplexer_1_out, multiplexer_2_out, multiplexer_3_out, multiplexer_4_out;

  Multiplexer multiplexer_1 (.in0(Y3), .in1(In3), .out(multiplexer_1_out), .sel(Load));
  Multiplexer multiplexer_2 (.in0(Y2), .in1(In2), .out(multiplexer_2_out), .sel(Load));
  Multiplexer multiplexer_3 (.in0(Y1), .in1(In1), .out(multiplexer_3_out), .sel(Load));
  Multiplexer multiplexer_4 (.in0(Y0), .in1(In0), .out(multiplexer_4_out), .sel(Load));
  FourBitRegister fourbitregister_1 (
    .In3(multiplexer_1_out), .In2(multiplexer_2_out), .In1(multiplexer_3_out), .In0(multiplexer_4_out),
    .Reset(Reset), .Clk(Clk), .Y3(Y3), .Y2(Y2), .Y1(Y1), .Y0(Y0));
endmodule
